# Fritzing sketch roomCapacityCounter (saved by Fritzing 0.9.3b)
breadboards: 1

parts:
  Raspberry_Pi1 = Raspberry Pi 2
  hc-sr1 = hc-sr04
  hc-sr2 = hc-sr04
  R1 = Resistor [tolerance=±5% resistance=220 package=THT]
  R2 = Resistor [tolerance=±5% resistance=220 package="1206 [SMD]"]
  R3 = Resistor [tolerance=±5% resistance=220 package="1206 [SMD]"]
  R4 = Resistor [tolerance=±5% resistance=220 package="1206 [SMD]"]

nets:
  N1: Raspberry_Pi1.GPIO21, R1.Pin_0, R2.Pin_0
  N2: Raspberry_Pi1.GPIO20, hc-sr1.Trig
  N3: Raspberry_Pi1.GND, R1.Pin_1, R3.Pin_1
  N4: Raspberry_Pi1.GPIO24, R4.Pin_1
  N5: Raspberry_Pi1.GPIO23, hc-sr2.Trig
  VCC: Raspberry_Pi1.5V, hc-sr1.VCC, hc-sr2.VCC
  N6: hc-sr1.Echo, R2.Pin_1
  N7: hc-sr2.Echo, R4.Pin_0
